# Fritzing sketch AEP-P1 (saved by Fritzing 0.9.3b)
breadboards: 1

parts:
  MCU = Arduino Uno (Rev3)
  LED1 = smd LED [color="Red (633nm)" package="0603 [SMD]"]
  R1 = Resistor [tolerance=±5% resistance=330 package="1206 [SMD]"]

nets:
  N1: MCU.D13/SCK, R1.Pin_0
  GND: MCU.GND, LED1.cathode
  N2: LED1.anode, R1.Pin_1
