# Fritzing sketch AEP-P2 (saved by Fritzing 0.9.3b)
breadboards: 1

parts:
  MCU = Arduino Uno (Rev3) - ICSP
  LED_CURRENT__LIMITER = Resistor [tolerance=±5% resistance=330 package="2512 [SMD]"]
  BUTTON_PULLDOWN_RESISTOR = Resistor [tolerance=±5% resistance=220 package="2512 [SMD]"]
  LED = LED - 3mm [color="Red (633nm)" package="3 mm [THT]"]
  SWITCH = Momentary Switch [package=ksa_sealed_tac_switch]

nets:
  N1: MCU.5V, SWITCH.2
  GND: MCU.GND, BUTTON_PULLDOWN_RESISTOR.Pin_0, LED.cathode
  N2: MCU.D12/MISO, SWITCH.3
  N3: MCU.D13/SCK, LED_CURRENT__LIMITER.Pin_0
  N4: LED_CURRENT__LIMITER.Pin_1, LED.anode
  N5: BUTTON_PULLDOWN_RESISTOR.Pin_1, SWITCH.1
