# Fritzing sketch AEP-P3 (saved by Fritzing 0.9.3b)
breadboards: 1

parts:
  MCU = Arduino Uno (Rev3)
  POT = POT [package=pot_alpha_rv16af-20]
  R1 = Resistor [tolerance=±5% resistance=220 package=THT]
  LCD = LCD screen

nets:
  N1: MCU.A0, POT.S
  N2: MCU.D11_PWM/MOSI, LCD.E
  N3: MCU.D12/MISO, LCD.RS
  GND: MCU.GND, POT.A, LCD.VSS, LCD.V0, LCD.R/W, LCD.LED-
  N4: MCU.D2, LCD.DB7
  N5: MCU.D3_PWM, LCD.DB6
  N6: MCU.D4, LCD.DB5
  N7: MCU.D5_PWM, LCD.DB4
  5V: MCU.5V, POT.E
  N8: R1.Pin_0, LCD.VDD
  N9: R1.Pin_1, LCD.LED+
