# Fritzing sketch AEP-P4 (saved by Fritzing 0.9.3b)
breadboards: 1

parts:
  Temperature_Sensor = TMP36 [package=to-92]
  MCU = Arduino Uno (Rev3)
  R1 = Resistor [tolerance=±5% resistance=220 package=THT]
  R2 = Resistor [tolerance=±5% resistance=220 package=THT]
  LED1 = LED - 5mm [color="Blue (525nm)" package="5 mm [THT]"]
  LED2 = LED - 5mm [color="Red (633nm)" package="5 mm [THT]"]

nets:
  5V: Temperature_Sensor.VCC, MCU.VIN
  N1: Temperature_Sensor.VOUT, MCU.A0
  GND: Temperature_Sensor.GND, LED1.cathode, LED2.cathode
  N2: MCU.D8, R1.Pin_0
  N3: MCU.D9_PWM, R2.Pin_0
  N4: R1.Pin_1, LED1.anode
  N5: R2.Pin_1, LED2.anode
