# Fritzing sketch AEP-P5 (saved by Fritzing 0.9.3b)
breadboards: 1

parts:
  Temperature_Sensor = TMP36 [package=to-92]
  MCU = Arduino Uno (Rev3)
  16x2 = LCD screen
  R1 = Resistor [tolerance=±5% resistance=220 package="2512 [SMD]"]
  R2 = Resistor [tolerance=±5% resistance=220 package="2512 [SMD]"]
  R3 = Resistor [tolerance=±5% resistance=220 package="2512 [SMD]"]
  R4 = Resistor [tolerance=±5% resistance=220 package="2512 [SMD]"]
  R5 = Resistor [tolerance=±5% resistance=220 package="2512 [SMD]"]
  R6 = Resistor [tolerance=±5% resistance=220 package="2512 [SMD]"]
  R7 = Resistor [tolerance=±5% resistance=220 package="2512 [SMD]"]
  LED1 = LED - 3mm [color="Blue (525nm)" package="3 mm [THT]"]
  LED2 = LED - 3mm [color="Blue (525nm)" package="3 mm [THT]"]
  LED3 = LED - 5mm [color="Blue (505nm)" package="5 mm [THT]"]
  LED4 = LED - 3mm [color="Blue (525nm)" package="3 mm [THT]"]
  LED5 = LED - 3mm [color="Blue (525nm)" package="3 mm [THT]"]
  LED6 = LED - 5mm [color="Blue (505nm)" package="5 mm [THT]"]

nets:
  5V: Temperature_Sensor.VCC, MCU.VIN, 16x2.VDD, R1.Pin_0
  N1: Temperature_Sensor.VOUT, MCU.A0
  GND: Temperature_Sensor.GND, MCU.GND, 16x2.VSS, 16x2.V0, 16x2.R/W, 16x2.LED-, LED1.cathode, LED2.cathode, LED3.cathode, LED4.cathode, LED5.cathode, LED6.cathode
  N2: MCU.D8, R5.Pin_0
  N3: MCU.D9_PWM, R4.Pin_0
  N4: MCU.D10_PWM/SS, R3.Pin_0
  N5: MCU.D11_PWM/MOSI, 16x2.E
  N6: MCU.D12/MISO, 16x2.RS
  N7: MCU.D13/SCK, R2.Pin_0
  N8: MCU.D2, 16x2.DB7
  N9: MCU.D3_PWM, 16x2.DB6
  N10: MCU.D4, 16x2.DB5
  N11: MCU.D5_PWM, 16x2.DB4
  N12: MCU.D6_PWM, R7.Pin_0
  N13: MCU.D7, R6.Pin_0
  N14: 16x2.LED+, R1.Pin_1
  N15: R2.Pin_1, LED4.anode
  N16: R3.Pin_1, LED5.anode
  N17: R4.Pin_1, LED6.anode
  N18: R5.Pin_1, LED1.anode
  N19: R6.Pin_1, LED2.anode
  N20: R7.Pin_1, LED3.anode
